# Fritzing sketch stepper (saved by Fritzing 0.9.2b)
circuit board: 8.46667cm x 5.64444cm
breadboards: 1

parts:
  Part1 = Arduino Uno (Rev3) - ICSP
  R1 = Resistor [tolerance=±5% resistance=330 package=THT]
  S1 = Pushbutton [package="[THT]"]
  LED1 = LED - 5mm [color="Red (633nm)" package="5 mm [THT]"]
  R2 = Resistor [tolerance=±5% resistance=10k package=THT]

nets:
  N1: Part1.5V, S1.Pin_3, S1.Pin_4
  N2: Part1.ICSP_SCK, Part1.D13/SCK, LED1.cathode
  N3: Part1.GND, R1.Pin_1, R2.Pin_1
  N4: Part1.D2, S1.Pin_1, S1.Pin_2, R2.Pin_0
  N5: R1.Pin_0, LED1.anode
